# Fritzing sketch relay (saved by Fritzing 0.9.0b)
breadboards: 1

parts:
  元件1 = Arduino Uno (Rev3)
  KY-1 = Keyes Relay [package=THT]

nets:
  N1: 元件1.D2, KY-1.signal
  N2: 元件1.5V, KY-1.power
  N3: 元件1.GND, KY-1.ground

notes:
  Ｓ或IN： 數位腳位
  ＋ ：5V
  － ：GND

custom parts:
  Keyes Relay: The Keyes 5V relay module is suitable for SCM development, home appliance control. It uses a 5V~12V TIL control signal which can control DC / AC signal.
