# Fritzing sketch relayLedOK (saved by Fritzing 0.9.0b)
breadboards: 1

parts:
  元件1 = Arduino Uno (Rev3)
  KY-1 = Keyes Relay [package=THT]
  R1 = Resistor [tolerance=±5% resistance=220 package=THT]
  LED1 = LED - 5mm [color="Red (633nm)" package="5 mm [THT]"]

nets:
  N1: 元件1.D2, KY-1.signal
  N2: 元件1.5V, KY-1.power, KY-1.C
  N3: 元件1.GND, KY-1.ground, LED1.cathode
  N4: KY-1.NO, R1.Pin_0
  N5: R1.Pin_1, LED1.anode

notes:
  Ｓ 數位腳位
  ＋ 5V
  － GND
  將繼電器想成「開關」
  所以C和NO兩條線可互換

custom parts:
  Keyes Relay: The Keyes 5V relay module is suitable for SCM development, home appliance control. It uses a 5V~12V TIL control signal which can control DC / AC signal.
