# Fritzing sketch relayLed浮球NotYet (saved by Fritzing 0.9.0b)
breadboards: 1

parts:
  元件1 = Arduino Uno (Rev3)
  R1 = Resistor [tolerance=±5% resistance=220 package=THT]
  LED1 = LED - 5mm [color="Red (633nm)" package="5 mm [THT]"]

nets:
  N1: 元件1.5V, R1.Pin_0
  N2: 元件1.GND, LED1.cathode
  N3: R1.Pin_1, LED1.anode

notes:
  未接小浮球
