# Fritzing sketch relayLed浮球OK (saved by Fritzing 0.9.0b)
breadboards: 1

parts:
  元件1 = Arduino Uno (Rev3)
  R1 = Resistor [tolerance=±5% resistance=220 package=THT]
  LED1 = LED - 5mm [color="Red (633nm)" package="5 mm [THT]"]
  C1 = Tantalum Capacitor [capacitance=1μF package="100 mil [THT, tantalum]"]

nets:
  N1: 元件1.5V, C1.-
  N2: 元件1.GND, LED1.cathode
  N3: R1.Pin_0, C1.+
  N4: R1.Pin_1, LED1.anode

notes:
  將小浮球想成開關即可
  (免程式碼)
  小浮球
