# Fritzing sketch 投幣機電路圖 (saved by Fritzing 0.9.0b)
perfboards: 1

parts:
  R6 = Resistor [tolerance=±5% resistance=220 package=THT]
  R7 = Photocell (LDR) [package=THT]  # not connected
  R8 = Photocell (LDR) [package=THT]  # not connected
  R3 = Photocell (LDR) [package=THT]
  R9 = Resistor [tolerance=±5% resistance=220 package=THT]  # not connected
  R10 = Resistor [tolerance=±5% resistance=220 package=THT]  # not connected
  RGB_SMD_LED1 = SMD RGB LED (WS2812) [package=5050]  # not connected

nets:
  N1: R6.Pin_0, R3.pin_0

notes:
  5V
  GND
  A2
  A1
  A0
  黑線為底連接線
  D2
  WS2812
