# Fritzing sketch 硬幣 (saved by Fritzing 0.9.0b)
perfboards: 1

parts:
  R6 = Resistor [tolerance=±5% resistance=220 package=THT]
  R7 = Photocell (LDR) [package=THT]  # not connected
  R8 = Photocell (LDR) [package=THT]  # not connected
  R3 = Photocell (LDR) [package=THT]
  R9 = Resistor [tolerance=±5% resistance=220 package=THT]  # not connected
  R10 = Resistor [tolerance=±5% resistance=220 package=THT]  # not connected

nets:
  N1: R6.Pin_0, R3.pin_0
